// Logisim project Timed_Traffic_Light_System.circ as structural Verilog
module Decimal_Display (
  output a,
  output b,
  output c,
  output d,
  output e,
  output f,
  output g
);

  wire and_1_out, and_2_out, clock_1_out, clock_2_out, nand_1_out, nand_2_out, nand_3_out, nand_4_out,
       nand_5_out, nand_6_out, nand_7_out, nand_8_out, nand_9_out, nand_10_out, nand_11_out, nand_12_out,
       nand_13_out, nand_14_out, nand_15_out, nand_16_out, nand_17_out, nand_18_out, nand_19_out,
       nand_20_out, nand_21_out, nand_22_out, nand_23_out, nand_24_out, nand_25_out, nand_26_out,
       nand_27_out, nand_29_out, nand_30_out, nand_31_out, nand_32_out, nand_33_out, nand_34_out,
       nand_35_out, nand_36_out, nand_37_out, nand_38_out, nand_39_out, nand_40_out, nand_41_out,
       nand_42_out, nand_43_out, not_1_out, t_ff_1_q, t_ff_1_qn, t_ff_2_q, t_ff_2_qn, t_ff_3_q, t_ff_4_q,
       t_ff_4_qn, t_ff_5_q;

  and and_1 (and_1_out, t_ff_3_q, t_ff_2_q);
  Clock clock_1 (.out(clock_1_out));
  T_Flip_Flop t_ff_1 (
    .clk(clock_1_out), .T(1'b1), .Q(t_ff_1_q), .Qn(t_ff_1_qn), .reset(and_1_out));  // open: preset, en
  T_Flip_Flop t_ff_2 (.clk(t_ff_1_qn), .T(1'b1), .Q(t_ff_2_q), .Qn(t_ff_2_qn), .reset(and_1_out));  // open: preset, en
  T_Flip_Flop t_ff_3 (.clk(t_ff_4_qn), .T(1'b1), .Q(t_ff_3_q), .reset(and_1_out));  // open: Qn, preset, en
  T_Flip_Flop t_ff_4 (.clk(t_ff_2_qn), .T(1'b1), .Q(t_ff_4_q), .Qn(t_ff_4_qn), .reset(and_1_out));  // open: preset, en
  nand nand_1 (nand_1_out, t_ff_4_q, t_ff_4_q);
  nand nand_2 (nand_2_out, t_ff_1_q, t_ff_1_q);
  nand nand_3 (nand_3_out, t_ff_2_q, t_ff_2_q);
  nand nand_4 (nand_4_out, t_ff_1_q, t_ff_1_q);
  nand nand_5 (nand_5_out, t_ff_1_q, t_ff_1_q);
  nand nand_6 (nand_6_out, t_ff_4_q, t_ff_4_q);
  nand nand_7 (nand_7_out, t_ff_4_q, t_ff_4_q);
  nand nand_8 (nand_8_out, t_ff_1_q, t_ff_1_q);
  nand nand_9 (nand_9_out, t_ff_4_q, t_ff_4_q);
  nand nand_10 (nand_10_out, t_ff_1_q, t_ff_1_q);
  nand nand_11 (nand_11_out, t_ff_2_q, t_ff_2_q);
  nand nand_12 (nand_12_out, t_ff_4_q, t_ff_4_q);
  nand nand_13 (nand_13_out, t_ff_1_q, t_ff_1_q);
  nand nand_14 (nand_14_out, t_ff_1_q, t_ff_1_q);
  nand nand_15 (nand_15_out, t_ff_2_q, t_ff_2_q);
  nand nand_16 (nand_16_out, t_ff_1_q, t_ff_1_q);
  nand nand_17 (nand_17_out, t_ff_2_q, t_ff_2_q);
  nand nand_18 (nand_18_out, t_ff_1_q, t_ff_1_q);
  nand nand_19 (nand_19_out, t_ff_4_q, t_ff_4_q);
  nand nand_20 (nand_20_out, t_ff_2_q, t_ff_2_q);
  nand nand_21 (nand_21_out, t_ff_1_q, t_ff_1_q);
  nand nand_22 (nand_22_out, nand_1_out, nand_2_out);
  nand nand_23 (nand_23_out, t_ff_2_q, t_ff_2_q);
  nand nand_24 (nand_24_out, t_ff_4_q, t_ff_1_q);
  nand nand_25 (nand_25_out, t_ff_3_q, t_ff_3_q);
  nand nand_26 (nand_26_out, nand_3_out, nand_4_out);
  nand nand_27 (nand_27_out, t_ff_2_q, t_ff_1_q);
  nand nand_28 (c, t_ff_2_q, nand_5_out, nand_6_out);
  nand nand_29 (nand_29_out, nand_7_out, nand_8_out);
  nand nand_30 (nand_30_out, nand_9_out, t_ff_2_q);
  nand nand_31 (nand_31_out, t_ff_2_q, nand_10_out);
  nand nand_32 (nand_32_out, t_ff_4_q, nand_11_out, t_ff_1_q);
  nand nand_33 (nand_33_out, t_ff_3_q, t_ff_3_q);
  nand nand_34 (nand_34_out, nand_12_out, nand_13_out);
  nand nand_35 (nand_35_out, t_ff_2_q, nand_14_out);
  nand nand_36 (nand_36_out, nand_15_out, nand_16_out);
  nand nand_37 (nand_37_out, t_ff_4_q, nand_17_out);
  nand nand_38 (nand_38_out, t_ff_4_q, nand_18_out);
  nand nand_39 (nand_39_out, t_ff_3_q, t_ff_3_q);
  nand nand_40 (nand_40_out, nand_19_out, t_ff_2_q);
  nand nand_41 (nand_41_out, t_ff_4_q, nand_20_out);
  nand nand_42 (nand_42_out, t_ff_4_q, nand_21_out);
  nand nand_43 (nand_43_out, t_ff_3_q, t_ff_3_q);
  nand nand_44 (a, nand_22_out, nand_23_out, nand_24_out, nand_25_out);
  nand nand_45 (b, t_ff_4_q, nand_26_out, nand_27_out);
  nand nand_46 (d, nand_29_out, nand_30_out, nand_31_out, nand_32_out, nand_33_out);
  nand nand_47 (e, nand_34_out, nand_35_out);
  nand nand_48 (f, nand_36_out, nand_37_out, nand_38_out, nand_39_out);
  nand nand_49 (g, nand_40_out, nand_41_out, nand_42_out, nand_43_out);
  _7_Segment_Display u_7_segment_display_1 (.g(g), .f(f), .a(a), .b(b), .e(e), .d(d), .c(c));  // open: dp
  Clock clock_2 (.out(clock_2_out));
  LED led_1 (.in(t_ff_5_q));
  LED led_2 (.in(t_ff_3_q));
  LED led_3 (.in(not_1_out));
  not not_1 (not_1_out, t_ff_5_q);
  T_Flip_Flop t_ff_5 (.clk(clock_2_out), .T(and_2_out), .Q(t_ff_5_q));  // open: Qn, preset, reset, en
  and and_2 (and_2_out, t_ff_1_q, t_ff_3_q);
endmodule
